# Fritzing sketch Schaltplan (saved by Fritzing 1.0.3b)
breadboards: 1

parts:
  RHT1 = Humidity and Temperature Sensor RHT03
  Raspberry_Pi_1 = Raspberry Pi 3 [part_number=RPI-3-V1.2]
  R1 = Photocell (LDR) [power=0.25W dark_resistance_@0.01lx=300kΩ light_resistance_@100lx=400Ω luminance=10lx package=THT]  # not connected
  ADC1 = MCP3008 [package=dil16]  # not connected

nets:
  VCC: RHT1.Vcc, Raspberry_Pi_1.3V3
  N1: RHT1.Data-signal, Raspberry_Pi_1.GPIO4
  N2: RHT1.GND_1, RHT1.GND_2, Raspberry_Pi_1.GND
